# Fritzing sketch Untitled Sketch 4 (saved by Fritzing 0.9.0b)
breadboards: 1

parts:
  LED1 = LED - 5mm [color="Green (570nm)" package="5 mm [THT]"]
  LED2 = LED - 5mm [color="Red (633nm)" package="5 mm [THT]"]
  R1 = Resistor [tolerance=±5% resistance=220 package=THT]
  S2 = Pushbutton [package="[THT]"]
  Parte2 = Arduino Uno (Rev3)
  R4 = Resistor [tolerance=±5% resistance=220 package=THT]
  R3 = Resistor [tolerance=±5% resistance=220 package=THT]
  S3 = Pushbutton [package="[THT]"]
  R6 = Resistor [tolerance=±5% resistance=220 package=THT]
  J1 = Basic Servo
  U1 = MLX90614 [package=to-39]

nets:
  N1: LED1.cathode, LED2.cathode, R3.Pin_0, U1.SCL_VZ
  N2: LED1.anode, R4.Pin_1
  N3: LED2.anode, R1.Pin_1
  N4: R1.Pin_0, Parte2.D6_PWM
  N5: S2.Pin_1, S2.Pin_2, R3.Pin_1
  N6: S2.Pin_3, S2.Pin_4, Parte2.D5_PWM, R6.Pin_0, U1.PWM_SDA
  N7: Parte2.D8, J1.pulse
  N8: Parte2.D9_PWM, U1.VSS
  N9: Parte2.D4, S3.Pin_3, S3.Pin_4
  N10: Parte2.D7, R4.Pin_0
  5V: Parte2.5V, J1.vcc
  GND: Parte2.GND, J1.gnd
  N11: S3.Pin_1, S3.Pin_2, R6.Pin_1
